# Fritzing sketch project1Fritzing (saved by Fritzing 0.9.3b)

parts:
  J1 = STM32 Nucleo boards
  RE1 = Rotary Encoder [package=THT]
  Grove1 = Grove Temperature Sensor
  Grove2 = Grove Light Sensor
  Componente1 = Breakout Board for Electret Microphone
  Grove3 = Grove Button
  M1 = DOIT Esp32 DevKit v1 (30 pins long, 11 pins width) [part_number=ESP32S-PIN30]  # not connected
  Componente2 = Bluetooth HC-05 Macho

nets:
  N1: J1.A0, RE1.EncoderPinA
  N2: J1.A1, Grove1.SIG
  N3: J1.A2, Grove2.SIG
  N4: J1.A3, Componente1.AUD
  N5: J1.D7, Grove3.SIG
  5V: J1.5V, Componente2.VCC
  GND: J1.GND, Componente2.GND
  N6: J1.PA15, Componente2.RXD
  N7: J1.PB7, Componente2.TXD

custom parts:
  DOIT Esp32 DevKit v1 (30 pins long, 11 pins width): The DOIT Esp32 DevKit v1 is one of the development board created by DOIT to evaluate the ESP-WROOM-32 module. It is based on the ESP32 microcontroller that boasts Wifi, Bluetooth, Ethernet and Low Power support all in a single chip. (vanepp) made breadboard work, adjusted pin numbering and labels and reduced size of schematic and cleaned up pcb. This chip is 30pins long (2 x15) and 11 pins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
