# Fritzing sketch Lab7Fritzing (saved by Fritzing 0.9.3b)
breadboards: 1

parts:
  R1 = Resistor [tolerance=±5% resistance=220 package=THT]
  R2 = Resistor [tolerance=±5% resistance=330 package=THT]
  R3 = Resistor [tolerance=±5% resistance=75 package=THT]
  LED1 = LED - 5mm [color="Green (570nm)" package="5 mm [THT]"]
  LED2 = LED - 5mm [color="Yellow (595nm)" package="5 mm [THT]"]
  LED3 = LED - 5mm [color="Red (633nm)" package="5 mm [THT]"]
  LED4 = LED - 5mm [color="Green (570nm)" package="5 mm [THT]"]
  LED5 = LED - 5mm [color="Red (633nm)" package="5 mm [THT]"]
  R4 = Resistor [tolerance=±5% resistance=220 package=THT]
  R5 = Resistor [tolerance=±5% resistance=75 package=THT]
  J1 = STM32 Nucleo boards
  Grove1 = Grove Button
  hc-sr1 = hc-sr04
  J2 = Piezo Speaker
  U1 = LCD-16X2 [package=lcd-16x2_noholes]
  M1 = DOIT Esp32 DevKit v1 (30 pins long, 11 pins width) [part_number=ESP32S-PIN30]

nets:
  N1: R1.Pin_0, J1.D13/SCK
  N2: R1.Pin_1, LED1.anode
  N3: R2.Pin_0, J1.D12/MISO
  N4: R2.Pin_1, LED2.anode
  N5: R3.Pin_0, J1.D11_PWM/MOSI
  N6: R3.Pin_1, LED3.anode
  N7: LED1.cathode, LED2.cathode, LED3.cathode, LED4.cathode, LED5.cathode, J1.GND#1188
  N8: LED4.anode, R4.Pin_1
  N9: LED5.anode, R5.Pin_1
  N10: R4.Pin_0, J1.D4
  N11: R5.Pin_0, J1.D2
  N12: J1.A0, J2.pin1
  N13: J1.D8, M1.RX2
  N14: J1.D9_PWM, hc-sr1.Trig, hc-sr1.Echo
  N15: J1.D1/TX, U1.VSS
  N16: J1.D6_PWM, Grove1.SIG
  5V: J1.5V, hc-sr1.VCC
  N17: J1.GND#1189, hc-sr1.GND

custom parts:
  DOIT Esp32 DevKit v1 (30 pins long, 11 pins width): The DOIT Esp32 DevKit v1 is one of the development board created by DOIT to evaluate the ESP-WROOM-32 module. It is based on the ESP32 microcontroller that boasts Wifi, Bluetooth, Ethernet and Low Power support all in a single chip. (vanepp) made breadboard work, adjusted pin numbering and labels and reduced size of schematic and cleaned up pcb. This chip is 30pins long (2 x15) and 11 pins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
