# Fritzing sketch project2Fritzing (saved by Fritzing 0.9.3b)
breadboards: 1

parts:
  M1 = DOIT Esp32 DevKit v1 (30 pins long, 11 pins width) [part_number=ESP32S-PIN30]
  M2 = DOIT Esp32 DevKit v1 (30 pins long, 11 pins width) [part_number=ESP32S-PIN30]
  Componente1 = Thumb Joystick
  J1 = Basic Servo
  J2 = Basic Servo

nets:
  VCC: M1.3V3, J1.vcc, J2.vcc
  GND: M1.GND, J1.gnd, J2.gnd
  N1: M1.D18, J1.pulse
  N2: M1.D21, J2.pulse
  3V3: M2.3V3, Componente1.VCC
  GND_2: M2.GND, Componente1.GND
  N3: M2.D14, Componente1.SEL
  N4: M2.D12, Componente1.VERT
  N5: M2.D13, Componente1.HORZ

notes:
  Servo eje X
  Servo eje Y

custom parts:
  DOIT Esp32 DevKit v1 (30 pins long, 11 pins width): The DOIT Esp32 DevKit v1 is one of the development board created by DOIT to evaluate the ESP-WROOM-32 module. It is based on the ESP32 microcontroller that boasts Wifi, Bluetooth, Ethernet and Low Power support all in a single chip. (vanepp) made breadboard work, adjusted pin numbering and labels and reduced size of schematic and cleaned up pcb. This chip is 30pins long (2 x15) and 11 pins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
